# Fritzing sketch board (saved by Fritzing 0.9.10b)
stripboards: 1

parts:
  Part1 = Arduino Uno (Rev3)
  U1 = 4001 4 x 2 Input NOR Gate, single part [part_number=4001 package="DIP (Dual Inline) [THT]"]
  R1 = Resistor [tolerance=±5% power=0.25 resistance=10 package=THT]
  R2 = Resistor [tolerance=±5% power=0.25 resistance=10 package=THT]
  R3 = Resistor [tolerance=±5% power=0.25 resistance=10 package=THT]
  D1 = Rectifier Diode [part_number=1N4001 package="300 mil [THT]"]
  R4 = Resistor [tolerance=±5% power=0.25 resistance=220 package=THT]
  R5 = Resistor [tolerance=±5% power=0.25 resistance=220 package=THT]
  LED1 = RGB LED (com. cathode, rgb) [package="5 mm [THT]"]
  R6 = Resistor [tolerance=±5% power=0.25 resistance=1M package=THT]
  VCC1 = Battery

nets:
  N1: Part1.A0, U1.VDD, R6.Pin_0, VCC1.+
  N2: Part1.D2, U1.B2, D1.cathode
  N3: Part1.D3_PWM, R4.Pin_0, R5.Pin_1
  N4: Part1.GND, U1.B1, R1.Pin_1, R2.Pin_1, R3.Pin_1, D1.anode
  N5: U1.GND, R1.Pin_0, R2.Pin_0, R3.Pin_0
  N6: U1.B4, LED1.common_cathode, R6.Pin_1, VCC1.-
  N7: R4.Pin_1, LED1.green_anode
  N8: R5.Pin_0, LED1.red_anode
